# Fritzing sketch schematic (saved by Fritzing 0.9.3b)
circuit board: 10cm x 10cm
breadboards: 1

parts:
  1k = Resistor [tolerance=±5% resistance=1k package=THT]
  U1 = Voltage Regulator - Variable [package="TO220 [THT]"]
  DS1 = DS18B20 1-Wire Temperature Sensor [part_number=DS18B20]
  WeMos_D1_Mini1 = WeMos D1 Mini
  330 = Resistor [tolerance=±5% resistance=330 package=THT]
  VIN = female pin header, 2 pins [form="♀ (female)"]
  R = MOSFET-NCHANNEL [package=to220v]
  LDR = Photocell (LDR) [package=THT]
  MOTION = female pin header, 3 pins [form="♀ (female)"]
  V1 = DC Power [voltage=12V]  # not connected
  B = MOSFET-NCHANNEL [package=to220v]
  G = MOSFET-NCHANNEL [package=to220v]
  W = MOSFET-NCHANNEL [package=to220v]
  4k7 = Resistor [tolerance=±5% resistance=4.7k package=THT]
  RGB_OUT = female pin header, 4 pins [form="♀ (female)"]
  WHITE = female pin header, 2 pins [form="♀ (female)"]
  100 = Resistor [tolerance=±5% resistance=100 package=THT]
  10k = Resistor [tolerance=±5% resistance=10k package=THT]
  100_2 = Resistor [tolerance=±5% resistance=100 package=THT]
  10k_2 = Resistor [tolerance=±5% resistance=10k package=THT]
  100_3 = Resistor [tolerance=±5% resistance=100 package=THT]
  10k_3 = Resistor [tolerance=±5% resistance=10k package=THT]
  MOTION_2 = female pin header, 3 pins [form="♀ (female)"]
  DHT22 = Humidity and Temperature Sensor RHT03
  4k7_2 = Resistor [tolerance=±5% resistance=4.7k package=THT]
  220k = Resistor [tolerance=±5% resistance=220k package=THT]
  10k_4 = Resistor [tolerance=±5% resistance=10k package=THT]
  100_4 = Resistor [tolerance=±5% resistance=100 package=THT]
  RGB2 = female pin header, 3 pins [form="♀ (female)"]
  BMP180 = rounded female pin header, 6 pins [form="♀ (female rounded)"]

nets (from the pcb view):
  N1: 1k.Pin_0, U1.ADJ, 330.Pin_1
  N2: 1k.Pin_1, DS1.GND, WeMos_D1_Mini1.G, VIN.pin2, R.S, LDR.pin_0, MOTION.pin3, B.S, G.S, W.S, 10k.Pin_1, 10k_2.Pin_1, 10k_3.Pin_1, MOTION_2.pin3, DHT22.GND_2, 10k_4.Pin_1, RGB2.pin3, BMP180.pin6
  VDD: U1.OUT, DS1.VDD, WeMos_D1_Mini1.5V, 330.Pin_0, MOTION.pin1, 4k7.Pin_0, MOTION_2.pin1, DHT22.Vcc, 4k7_2.Pin_1, 220k.Pin_0, BMP180.pin1
  N3: U1.IN, VIN.pin1, RGB_OUT.pin1, WHITE.pin1, RGB2.pin2
  N4: DS1.DQ, WeMos_D1_Mini1.D7, 4k7.Pin_1
  N5: WeMos_D1_Mini1.A0, LDR.pin_1, 220k.Pin_1
  N6: WeMos_D1_Mini1.D1, 100.Pin_0, 10k.Pin_0
  N7: WeMos_D1_Mini1.D2, 100_3.Pin_0, 10k_3.Pin_0, RGB2.pin1
  N8: WeMos_D1_Mini1.D3, 100_2.Pin_0, 10k_2.Pin_0
  N9: WeMos_D1_Mini1.D4, 10k_4.Pin_0, 100_4.Pin_0
  N10: WeMos_D1_Mini1.D5, DHT22.Data-signal, 4k7_2.Pin_0
  N11: WeMos_D1_Mini1.D6, MOTION.pin2
  N12: WeMos_D1_Mini1.D8, MOTION_2.pin2
  N13: WeMos_D1_Mini1.RX, BMP180.pin2
  N14: WeMos_D1_Mini1.TX, BMP180.pin3
  N15: R.G, 100_3.Pin_1
  N16: R.D, RGB_OUT.pin2
  N17: B.G, 100_2.Pin_1
  N18: B.D, RGB_OUT.pin3
  N19: G.G, 100_4.Pin_1
  N20: G.D, RGB_OUT.pin4
  N21: W.G, 100.Pin_1
  N22: W.D, WHITE.pin2

notes:
  - +
  + -
  G B R +
  bedlight v1
  - + D
  LDR
  + D -
